// Digital circuit alu_math.dig as structural Verilog
module alu_math (
  input  in_1,
  input  in_2,
  input  in_3,
  input  in_4,
  input  in_5,
  input  in_6,
  input  in_7,
  input  in_8,
  input  in_9,
  input  in_10,
  input  in_11,
  input  in_12,
  input  in_13,
  input  in_14,
  input  in_15,
  input  in_16,
  input  in_17,
  input  [2:0] in_18,
  input  in_20,
  output [7:0] out_19,
  output [7:0] out_21
);

  wire _74283_1_pin9, B0INV, B1INV, B2INV, B3INV, B4INV, B5INV, B6INV, B7INV, CARRY_OUT, or_9_out, ZERO_OUT;
  wire [7:0] ADD_SUB, AND, NOT, OR, XOR;

  Multiplexer #(.Selector_Bits(3), .Bits(8)) multiplexer_1 (
    .sel(in_18), .in_0(ADD_SUB), .in_1(AND), .in_2(OR), .in_3(XOR), .in_4(NOT),
    .in_5({1'b0, in_8, in_7, in_6, in_5, in_4, in_3, in_2}), .in_6({8{1'b0}}), .in_7({8{1'b0}}), .out(out_19));
  not not_1 (NOT[0], in_1);
  not not_2 (NOT[1], in_2);
  not not_3 (NOT[2], in_3);
  not not_4 (NOT[3], in_4);
  not not_5 (NOT[4], in_5);
  not not_6 (NOT[5], in_6);
  not not_7 (NOT[6], in_7);
  not not_8 (NOT[7], in_8);
  xor xor_1 (XOR[0], in_1, in_9);
  xor xor_2 (XOR[1], in_2, in_10);
  xor xor_3 (XOR[2], in_3, in_11);
  xor xor_4 (XOR[3], in_4, in_12);
  xor xor_5 (XOR[4], in_5, in_13);
  xor xor_6 (XOR[5], in_6, in_14);
  xor xor_7 (XOR[6], in_7, in_15);
  xor xor_8 (XOR[7], in_8, in_16);
  and and_1 (AND[0], in_1, in_9);
  and and_2 (AND[1], in_2, in_10);
  and and_3 (AND[2], in_3, in_11);
  and and_4 (AND[3], in_4, in_12);
  and and_5 (AND[4], in_5, in_13);
  and and_6 (AND[5], in_6, in_14);
  and and_7 (AND[6], in_7, in_15);
  and and_8 (AND[7], in_8, in_16);
  or or_1 (OR[0], in_1, in_9);
  or or_2 (OR[1], in_2, in_10);
  or or_3 (OR[2], in_3, in_11);
  or or_4 (OR[3], in_4, in_12);
  or or_5 (OR[4], in_5, in_13);
  or or_6 (OR[5], in_6, in_14);
  or or_7 (OR[6], in_7, in_15);
  or or_8 (OR[7], in_8, in_16);
  _74283 _74283_1 (
    .pin1(ADD_SUB[1]), .pin2(B1INV), .pin3(in_2), .pin4(ADD_SUB[0]), .pin5(in_1), .pin6(B0INV), .pin7(in_17),
    .pin8(1'b0), .pin9(_74283_1_pin9), .pin10(ADD_SUB[3]), .pin11(B3INV), .pin12(in_4), .pin13(ADD_SUB[2]),
    .pin14(in_3), .pin15(B2INV), .pin16(1'b1));
  or or_9 (or_9_out, out_19[0], out_19[1], out_19[2], out_19[3], out_19[4], out_19[5], out_19[6], out_19[7]);
  not not_9 (ZERO_OUT, or_9_out);
  xor xor_9 (B0INV, in_9, in_17);
  xor xor_10 (B1INV, in_10, in_17);
  xor xor_11 (B2INV, in_11, in_17);
  xor xor_12 (B3INV, in_12, in_17);
  xor xor_13 (B4INV, in_13, in_17);
  xor xor_14 (B5INV, in_14, in_17);
  xor xor_15 (B6INV, in_15, in_17);
  xor xor_16 (B7INV, in_16, in_17);
  _74283 _74283_2 (
    .pin1(ADD_SUB[5]), .pin2(B5INV), .pin3(in_6), .pin4(ADD_SUB[4]), .pin5(in_5), .pin6(B4INV),
    .pin7(_74283_1_pin9), .pin8(1'b0), .pin9(CARRY_OUT), .pin10(ADD_SUB[7]), .pin11(B7INV), .pin12(in_8),
    .pin13(ADD_SUB[6]), .pin14(in_7), .pin15(B6INV), .pin16(1'b1));
  assign out_21 = in_20 ? out_19 : 8'bz;  // Driver driver_1

  // Other names for the same wires on the sheet: A0 = in_1; A1 = in_2;
  //   SHR_OUT[6:0] = {in_8, in_7, in_6, in_5, in_4, in_3, in_2}; A2 = in_3; A3 = in_4; A4 = in_5; A5 = in_6;
  //   A6 = in_7; A7 = in_8; ALU_OUT = in_20; ALU_RESULT[7:0] = out_19; NEG_OUT = out_19[7]; ALU_SEL[2:0] = in_18;
  //   B0 = in_9; B1 = in_10; B2 = in_11; B3 = in_12; B4 = in_13; B5 = in_14; B6 = in_15; B7 = in_16;
  //   BUS[7:0] = out_21; SUB = in_17
endmodule
