// Digital circuit clock.dig as structural Verilog
module clock (
  input  Clock,
  input  STEP,
  input  RESET,
  input  MODE_SELECT,
  output SYS_CLK
);

  wire not_1_out, not_2_out, Q, Q_t;

  not not_1 (not_1_out, STEP);
  not not_2 (not_2_out, RESET);
  nand nand_1 (Q, not_1_out, Q_t);
  nand nand_2 (Q_t, Q, not_2_out);
  Multiplexer multiplexer_1 (.sel(MODE_SELECT), .in_0(Clock), .in_1(Q), .out(SYS_CLK));
endmodule
