// Digital circuit full_adder.dig as structural Verilog
module full_adder (
  input  A,
  input  B,
  input  C,
  output SUM___A_XOR_B__XOR__Cin,
  output CARRY_OUT___A_AND_B__OR__CIN_AND__A_XOR_B
);

  wire and_1_out, and_2_out, xor_1_out;

  xor xor_1 (xor_1_out, A, B);
  and and_1 (and_1_out, B, A);
  and and_2 (and_2_out, xor_1_out, C);
  xor xor_2 (SUM___A_XOR_B__XOR__Cin, xor_1_out, C);
  or or_1 (CARRY_OUT___A_AND_B__OR__CIN_AND__A_XOR_B, and_2_out, and_1_out);
endmodule
