// Digital circuit register.dig as structural Verilog
module register (
  input  [7:0] DATA_IN,
  input  REG_IN,
  input  CLK,
  input  REG_OUT,
  output [7:0] DATA_OUT,
  output [7:0] PROBE
);

  Register #(.Bits(8)) register_1 (.D(DATA_IN), .C(CLK), .en(REG_IN), .Q(PROBE));
  assign DATA_OUT = REG_OUT ? PROBE : 8'bz;  // Driver driver_1
endmodule
