// Digital circuit sap-x-main.dig as structural Verilog
module sap_x_main (
  input  A_IN,
  input  A_OUT,
  input  B_IN,
  input  B_OUT,
  input  C_IN,
  input  C_OUT,
  input  TMP_IN,
  input  TMP_OUT,
  input  CLK,
  input  STEP,
  input  RESET,
  input  MODE_SELECT,
  input  [7:0] in_13,
  input  MANUAL_IN,
  input  MAR_IN,
  input  RAM_IN,
  input  RAM_OUT
);

  wire clock_1_sys_clk, MAR_p9;
  wire [7:0] MAR_p3, MAR_p8, ramdualport_1_d;

  clock clock_1 (.Clock(CLK), .STEP(STEP), .RESET(RESET), .MODE_SELECT(MODE_SELECT), .SYS_CLK(clock_1_sys_clk));
  register Register_A (.DATA_IN(MAR_p3), .REG_IN(A_IN), .REG_OUT(clock_1_sys_clk));  // open: CLK, DATA_OUT, PROBE
  register Register_B (.DATA_IN(MAR_p3), .REG_IN(B_IN), .REG_OUT(clock_1_sys_clk));  // open: CLK, DATA_OUT, PROBE
  register Register_C (.DATA_IN(MAR_p3), .REG_IN(C_IN), .REG_OUT(clock_1_sys_clk));  // open: CLK, DATA_OUT, PROBE
  register TMP_Register (.DATA_IN(MAR_p3), .REG_IN(TMP_IN), .REG_OUT(clock_1_sys_clk));  // open: CLK, DATA_OUT, PROBE
  // register MAR: pin names not known; wires that end beside it: C_OUT, TMP_OUT, MAR_p3, MAR_IN, clock_1_sys_clk, 1'b1, MAR_p3, MAR_p8, MAR_p9, MAR_p3
  // NotConnected on MAR_p9
  RAMDualPort #(.AddrBits(8), .Bits(8)) ramdualport_1 (
    .A(MAR_p8), .Din(MAR_p3), .str(RAM_IN), .C(clock_1_sys_clk), .ld(1'b1), .D(ramdualport_1_d));
  assign MAR_p3 = RAM_OUT ? ramdualport_1_d : 8'bz;  // Driver driver_1
  assign MAR_p3 = MANUAL_IN ? in_13 : 8'bz;  // Driver driver_2
endmodule
